// Logisim project offline1.circ as structural Verilog: 3 circuits, main circuit main
module main (
  input  A,
  input  B,
  input  C,
  output out_4
);

  wire n7408_1_p3;

  // _7408 7408_1: pin names not known; wires that end beside it: C, A, n7408_1_p3, 1'b0, 1'b1
  // _7432 7432_1: pin names not known; wires that end beside it: B, C, n7408_1_p3, B, out_4, 1'b0, 1'b1

  // Notes on the sheet:
  //   B+AC
endmodule

module problem2 (
  input  A,
  input  B,
  input  C,
  output out_4
);

  wire n7404_1_p2, n7408_1_p3;

  // _7404 7404_1: pin names not known; wires that end beside it: C, n7404_1_p2, 1'b0, 1'b1
  // _7408 7408_1: pin names not known; wires that end beside it: A, n7404_1_p2, n7408_1_p3, 1'b0, 1'b1
  // _7432 7432_1: pin names not known; wires that end beside it: n7404_1_p2, n7408_1_p3, B, out_4, 1'b0, 1'b1

  // Notes on the sheet:
  //   B+AC'
endmodule

module problem3 (
  input  X,
  input  Y,
  input  Z,
  output out_4
);

  wire n7432_1_p3, n7432_1_p5;

  // _7432 7432_1: pin names not known; wires that end beside it: Y, Z, n7432_1_p3, X, n7432_1_p5, out_4, 1'b1
  // _7404 7404_1: pin names not known; wires that end beside it: Y, Z, 1'b0, n7432_1_p3, n7432_1_p5, 1'b0, 1'b1

  // Notes on the sheet:
  //   X+(Y+Z)'
endmodule
