// Logisim project 2105166.circ as structural Verilog: 2 circuits, main circuit main
module main (
  input  in_1,
  input  in_2,
  input  in_3,
  input  in_4,
  output out_5
);

  wire n7404_1_p2, n7404_1_p4, n7408_1_p3;

  // _7404 7404_1: pin names not known; wires that end beside it: in_1, n7404_1_p2, in_1, n7404_1_p4, 1'b0, 1'b1
  // _7408 7408_1: pin names not known; wires that end beside it: n7404_1_p2, n7404_1_p4, n7408_1_p3, out_5, 1'b0, 1'b1
  // _7432 7432_1: pin names not known; wires that end beside it: n7408_1_p3, 1'b0, 1'b1

  assign in_3 = in_1;

  // Notes on the sheet:
  //   A
  //   B
  //   C
  //   D
  //   f=A'C'+AC
endmodule

module problem2 (
  input  in_1,
  input  in_2,
  input  in_3,
  input  in_4,
  input  in_5,
  output out_6
);

  wire n7404_1_p2, n7404_1_p4, n7404_1_p6, n7408_1_p3, n7408_1_p6, n7408_1_p11;

  // _7404 7404_1: pin names not known; wires that end beside it: in_3, n7404_1_p2, in_1, n7404_1_p4, in_4, n7404_1_p6, 1'b0, 1'b1
  // _7408 7408_1: pin names not known; wires that end beside it: in_1, n7404_1_p2, n7408_1_p3, n7404_1_p4, in_3, n7408_1_p6, 1'b0, 1'b1, n7408_1_p6, n7404_1_p6, n7408_1_p11
  // _7432 7432_1: pin names not known; wires that end beside it: n7408_1_p3, n7408_1_p11, out_6, 1'b0, 1'b1

  // Notes on the sheet:
  //   A
  //   B
  //   C
  //   D
  //   E
  //   f=AC'+A'CD'
endmodule
