// Logisim project 2105166.circ as structural Verilog: 1 circuit, main circuit main
module main (
  input  P,
  input  in_2,
  input  R,
  output out_4,
  output B
);

  wire n7404_1_p2, n7404_1_p4, n7408_1_p3, n7408_1_p6, n7486_1_p3;

  // _7486 7486_1: pin names not known; wires that end beside it: P, in_2, n7486_1_p3, n7486_1_p3, R, out_4, 1'b0, 1'b1
  // _7404 7404_1: pin names not known; wires that end beside it: P, n7404_1_p2, n7486_1_p3, n7404_1_p4, 1'b0, 1'b1
  // _7408 7408_1: pin names not known; wires that end beside it: n7404_1_p2, in_2, n7408_1_p3, n7404_1_p4, R, n7408_1_p6, 1'b0, 1'b1
  // _7432 7432_1: pin names not known; wires that end beside it: n7408_1_p3, n7408_1_p6, B, 1'b0, 1'b1

  // Notes on the sheet:
  //   Q
  //   D
endmodule
