// Logisim project 2105166_ONLINE1.circ as structural Verilog: 1 circuit, main circuit main
module main (
  input  A,
  input  in_2,
  input  in_3,
  input  D,
  output out_5
);

  wire n7404_1_p2, n7404_1_p4, n7432_1_p3, n7432_1_p5;

  // _7404 7404_1: pin names not known; wires that end beside it: in_3, n7404_1_p2, A, n7404_1_p4, 1'b0, 1'b1
  // _7432 7432_1: pin names not known; wires that end beside it: in_2, n7404_1_p2, n7432_1_p3, n7432_1_p3, n7432_1_p5, out_5, 1'b0, 1'b1
  // _7408 7408_1: pin names not known; wires that end beside it: n7404_1_p4, D, n7432_1_p5, 1'b0, 1'b1

  // Notes on the sheet:
  //   Problem 3
  //   B
  //   C
  //   B+C'+A'D'
endmodule
