// Logisim project 2105166.circ as structural Verilog: 1 circuit, main circuit main
module main (
  input  x1,
  input  x2,
  input  x3,
  input  x4,
  input  y1,
  input  y2,
  input  y3,
  input  y4,
  input  in_9,
  input  c0,
  output f1,
  output f2,
  output f3,
  output f4
);

  wire n7483_1_p4, n7483_1_p6, n7483_1_p7, n7483_1_p10;

  // _7483 7483_1: pin names not known; wires that end beside it: x4, f3, x3, n7483_1_p4, f2, n7483_1_p6, n7483_1_p7, f4, c0, n7483_1_p10, x1, f1
  // _7486 7486_1: pin names not known; wires that end beside it: y1, in_9, n7483_1_p10, y2, in_9, n7483_1_p6, y4, in_9, n7483_1_p7, in_9, y3, n7483_1_p4, x2

  // Notes on the sheet:
  //   c1
endmodule
